# Fritzing sketch conexiones (saved by Fritzing 0.9.3b)
breadboards: 1

parts:
  Part1 = Arduino Nano (Rev3.0) (ICSP)
  R1 = Resistor [tolerance=±5% resistance=22k package="1206 [SMD]"]
  R2 = Resistor [tolerance=±5% resistance=22k package="1206 [SMD]"]
  R3 = Resistor [tolerance=±5% resistance=22k package="1206 [SMD]"]
  LED1 = LED - 5mm [color="Red (633nm)" package="5 mm [THT]"]

nets:
  N1: Part1.GND, LED1.anode
  N2: Part1.D2, R3.Pin_0
  N3: Part1.5V, R1.Pin_1, R2.Pin_1
  N4: Part1.A1, R2.Pin_0
  N5: Part1.A0, R1.Pin_0

notes:
  Tapete metalico
  Cables que toca el usuario. Cada hilo hace un sonido distinto
  Hilo 0
  Hilo 1
  Led que enciende cuando Hilo 1 es tocado
  Las resistencias son de 22 k ohm
